# Fritzing sketch DMN_Version_1.5 (saved by Fritzing 0.9.3b)
breadboards: 1

parts:
  Raspberry_Pi_1 = Raspberry Pi 3 [part_number=RPI-3-V1.2]
  M1 = 1 chan 5v relay module
  VCC1 = Battery
  L1 = Solenoid
  PIR1 = PIR sensor
  S2 = Momentary Switch [package=ksa_sealed_tac_switch]
  R15 = Resistor [tolerance=±5% resistance=1k package=THT]
  Raspberry_Pi_2 = Raspberry Pi 3 [part_number=RPI-3-V1.2]
  R17 = Resistor [tolerance=±5% resistance=220 package=THT]
  J2 = Piezo Speaker
  R18 = Resistor [tolerance=±5% resistance=220 package=THT]
  LED1 = LED - 3mm [color="Red (633nm)" package="3 mm [THT]"]

nets:
  N1: Raspberry_Pi_1.3v3, M1.pin_1
  N2: Raspberry_Pi_1.GIPO27, PIR1.SIG
  GND: Raspberry_Pi_1.GND, M1.pin_2, PIR1.GND
  N3: Raspberry_Pi_1.GIPO18, M1.pin_3
  5V: Raspberry_Pi_1.5V, PIR1.VDD
  N4: M1.pin_4, VCC1.+
  N5: M1.pin_5, L1.pin2
  N6: S2.2, Raspberry_Pi_2.GIPO15
  N7: S2.4, R15.Pin_1
  N8: R15.Pin_0, Raspberry_Pi_2.3v3
  N9: Raspberry_Pi_2.GIPO22, R18.Pin_0
  N10: Raspberry_Pi_2.GIPO21, R17.Pin_1
  N11: Raspberry_Pi_2.GIPO23, Raspberry_Pi_2.GND, J2.pin1, LED1.anode
  N12: R17.Pin_0, J2.pin2
  N13: R18.Pin_1, LED1.cathode

notes:
  Plug camera into camera port
  Plug official power supply
  Connect speaker via aux cable
  5v relay single channel relay
  Connect finger scanner via uart USB attachment
  Piezo buzzer, 220 ohm resistor
  momentary switch, connected to 3.3v power, 1 Kilo ohm resistor, connected to gpio, Responsible for input from user inside the room
  In the real version, a 12v dc power supply is used
  12v sub-600 mA electric strike lock
  PIR sensor
  door sensor (represented as wires, yellow is the door components itself)
  led to indicate door open or closed
  Raspberry Pi Inside the room
  Raspberry Pi Outside the room

custom parts:
  1 chan 5v relay module: 1 Channel 5V Relay Module Board Shield with Optocoupler Support High and Low Level Trigger for Arduino.
